// Logisim project cpu.circ as structural Verilog: 4 circuits, main circuit main
module main (
  input  [31:0] INSTRUCTION,
  input  in_2,
  output [31:0] FETCH_ADDRESS,
  output [31:0] ra,
  output [31:0] sp,
  output [31:0] t0,
  output [31:0] t1,
  output [31:0] t2,
  output [31:0] s0,
  output [31:0] s1,
  output [31:0] a0
);

  wire ASel, branchcomp_1_breq, branchcomp_1_brlt, BrUn, BSel, comparator_1_eq, ControlLogic_memrw,
       ControlLogic_regwen, HS, PCSel, RegWEn;
  wire [1:0] ControlLogic_wbsel;
  wire [2:0] mydecoder_1_funct3, mydecoder_1_optype;
  wire [3:0] ALUSel;
  wire [4:0] mydecoder_1_rd, mydecoder_1_rs1, mydecoder_1_rs2, register_1_q, register_3_q;
  wire [6:0] mydecoder_1_funct7, mydecoder_1_opcode;
  wire [31:0] alu, DMEM_read_data, imm, multiplexer_1_out, multiplexer_2_out, multiplexer_3_out,
       multiplexer_4_out, multiplexer_5_out, pc, pc4, RegFile_read_data_1, RegFile_read_data_2, WriteBack;

  Register #(.width(32)) u_PC (.D(multiplexer_1_out), .clk(in_2), .Q(FETCH_ADDRESS));  // open: en, clr
  Multiplexer #(.width(32), .enable("false")) multiplexer_1 (
    .in0(alu), .in1(pc4), .out(multiplexer_1_out), .sel(PCSel));
  myDecoder mydecoder_1 (
    .DecoderIn(INSTRUCTION), .opcode(mydecoder_1_opcode), .funct7(mydecoder_1_funct7), .rs1(mydecoder_1_rs1),
    .rs2(mydecoder_1_rs2), .rd(mydecoder_1_rd), .funct3(mydecoder_1_funct3), .imm(imm),
    .opType(mydecoder_1_optype));
  Register #(.width(5)) register_1 (.D(mydecoder_1_rd), .clk(in_2), .Q(register_1_q));  // open: en, clr
  Adder #(.width(32)) adder_1 (.a(32'h1), .b(FETCH_ADDRESS), .out(pc4));  // open: cin, cout
  Register #(.width(32)) register_2 (.D(FETCH_ADDRESS), .clk(in_2), .Q(pc));  // open: en, clr
  // Probe on mydecoder_1_rs1
  // Probe on mydecoder_1_rs2
  // Probe on register_3_q
  Register #(.width(5)) register_3 (.D(mydecoder_1_rd), .clk(in_2), .Q(register_3_q));  // open: en, clr
  Comparator #(.width(5)) comparator_1 (.a(register_1_q), .b(mydecoder_1_rs1), .eq(comparator_1_eq));  // open: gt, lt
  not not_1 (HS, comparator_1_eq);
  // Probe on INSTRUCTION
  // Probe on WriteBack
  // Probe on RegWEn
  Register #(.width(32)) register_4 ();  // open: D, en, Q, clk, clr
  myController ControlLogic (
    .Inst32(INSTRUCTION), .opcode(mydecoder_1_opcode), .funct7(mydecoder_1_funct7),
    .funct3(mydecoder_1_funct3), .opType(mydecoder_1_optype), .BrEq(branchcomp_1_breq),
    .BrLT(branchcomp_1_brlt), .BSel(BSel), .PCSel(PCSel), .BrUn(BrUn), .ASel(ASel),
    .RegWEn(ControlLogic_regwen), .MemRW(ControlLogic_memrw), .WBSel(ControlLogic_wbsel), .ALUSel(ALUSel));
  regfile_main RegFile (
    .Read_Register_1_rs1(mydecoder_1_rs1), .Read_Register_2_rs2(mydecoder_1_rs2),
    .Write_Register_rd(register_3_q), .Write_Data(WriteBack), .Write_Enable(RegWEn), .Clock(in_2),
    .Read_Data_1(RegFile_read_data_1), .Read_Data_2(RegFile_read_data_2), .ra(ra), .sp(sp), .t0(t0), .t1(t1),
    .t2(t2), .s0(s0), .s1(s1), .a0(a0));
  // Probe on ALUSel
  Multiplexer #(.width(32), .enable("false")) multiplexer_2 (
    .in0(WriteBack), .in1(RegFile_read_data_1), .out(multiplexer_2_out), .sel(HS));
  // Probe on multiplexer_3_out
  Multiplexer #(.width(32), .enable("false")) multiplexer_3 (
    .in0(multiplexer_2_out), .in1(pc), .out(multiplexer_3_out), .sel(ASel));
  // Probe on multiplexer_4_out
  Multiplexer #(.width(32), .enable("false")) multiplexer_4 (
    .in0(RegFile_read_data_2), .in1(imm), .out(multiplexer_4_out), .sel(BSel));
  BranchComp branchcomp_1 (
    .DataA(RegFile_read_data_1), .DataB(RegFile_read_data_2), .BrUn(BrUn), .BrEq(branchcomp_1_breq),
    .BrLT(branchcomp_1_brlt));
  // Probe on RegFile_read_data_2
  Register #(.width(1)) register_5 (.D(ControlLogic_regwen), .clk(in_2), .Q(RegWEn));  // open: en, clr
  alu Arithmetic_Logic_Unit (.A(multiplexer_3_out), .B(multiplexer_4_out), .ALUSel(ALUSel), .Result(alu));
  // Probe on alu
  mem_main DMEM (
    .Address(alu), .Write_Data(RegFile_read_data_2), .Write_En(ControlLogic_memrw),
    .Read_Data(DMEM_read_data), .clk(in_2));
  // Probe on alu
  // Probe on DMEM_read_data
  // Probe on pc4
  Multiplexer #(.select(2), .width(32), .enable("false")) multiplexer_5 (
    .in0(alu), .in1(DMEM_read_data), .in2(pc4), .out(multiplexer_5_out), .sel(ControlLogic_wbsel));  // open: in3
  // Probe on ControlLogic_wbsel
  Register #(.width(32)) register_6 (.D(multiplexer_5_out), .clk(in_2), .Q(WriteBack));  // open: en, clr

  // Other names for the same wires on the sheet: clk = in_2; fetch_addr[31:0] = FETCH_ADDRESS

  // Notes on the sheet:
  //   Output
  //   Inputs/Outputs from run.circ. DO NOT MOVE THESE.
  //   Inputs
  //   Inputs/Outputs from run.circ. DO NOT MOVE THESE.
endmodule

module myDecoder (
  input  [31:0] DecoderIn,
  output [6:0] opcode,
  output [6:0] funct7,
  output [4:0] rs1,
  output [4:0] rs2,
  output [4:0] rd,
  output [2:0] funct3,
  output [31:0] imm,
  output [2:0] opType
);

  wire comparator_1_eq, comparator_2_eq, comparator_3_eq, comparator_4_eq, comparator_5_eq, comparator_6_eq,
       comparator_7_eq, comparator_8_eq;
  wire [31:0] I, S, SB, UJ;

  assign S = {{20{1'b0}}, {DecoderIn[31:25], DecoderIn[11:7]}};  // Bit_Extender bit_extender_1
  assign I = {{20{1'b0}}, DecoderIn[31:20]};  // Bit_Extender bit_extender_2
  assign SB = {{19{1'b0}}, {DecoderIn[31], DecoderIn[7], DecoderIn[30:25], DecoderIn[11:8], 1'b0}};  // Bit_Extender bit_extender_3
  Comparator #(.width(7), .mode("unsigned")) comparator_1 (
    .a(DecoderIn[6:0]), .b(7'b0000011), .eq(comparator_1_eq));  // open: gt, lt
  Comparator #(.width(7), .mode("unsigned")) comparator_2 (
    .a(DecoderIn[6:0]), .b(7'b0010011), .eq(comparator_2_eq));  // open: gt, lt
  Comparator #(.width(7), .mode("unsigned")) comparator_3 (
    .a(DecoderIn[6:0]), .b(7'b0100011), .eq(comparator_3_eq));  // open: gt, lt
  Comparator #(.width(7), .mode("unsigned")) comparator_4 (
    .a(DecoderIn[6:0]), .b(7'b0110011), .eq(comparator_4_eq));  // open: gt, lt
  assign UJ = {{11{1'b0}}, {DecoderIn[31], DecoderIn[19:12], DecoderIn[20], DecoderIn[30:21], 1'b0}};  // Bit_Extender bit_extender_4
  Comparator #(.width(7), .mode("unsigned")) comparator_5 (
    .a(DecoderIn[6:0]), .b(7'b1100011), .eq(comparator_5_eq));  // open: gt, lt
  Comparator #(.width(7), .mode("unsigned")) comparator_6 (
    .a(DecoderIn[6:0]), .b(7'b0110111), .eq(comparator_6_eq));  // open: gt, lt
  Comparator #(.width(7), .mode("unsigned")) comparator_7 (
    .a(DecoderIn[6:0]), .b(7'b1101111), .eq(comparator_7_eq));  // open: gt, lt
  Comparator #(.width(7), .mode("unsigned")) comparator_8 (
    .a(DecoderIn[6:0]), .b(7'b1100111), .eq(comparator_8_eq));  // open: gt, lt
  Multiplexer #(.select(3), .width(32), .enable("false")) multiplexer_1 (
    .in0(SB), .in1({DecoderIn[31:12], {12{1'b0}}}), .in2(UJ), .in3(I), .in4(I), .in5(I), .in6(S),
    .in7({32{1'b0}}), .out(imm), .sel(opType));
  Priority_Encoder priority_encoder_1 (
    .in0(comparator_5_eq), .in1(comparator_6_eq), .in2(comparator_7_eq), .in3(comparator_8_eq),
    .in4(comparator_1_eq), .in5(comparator_2_eq), .in6(comparator_3_eq), .in7(comparator_4_eq), .out(opType));  // open: en_in, gs, en_out

  assign funct3 = DecoderIn[14:12];
  assign funct7 = DecoderIn[31:25];
  assign opcode = DecoderIn[6:0];
  assign rd = DecoderIn[11:7];
  assign rs1 = DecoderIn[19:15];
  assign rs2 = DecoderIn[24:20];

  // Other names for the same wires on the sheet: DecoderInput[31:0] = DecoderIn; U[31:12] = DecoderIn[31:12]
endmodule

module myController (
  input  [31:0] Inst32,
  input  [6:0] opcode,
  input  [6:0] funct7,
  input  [2:0] funct3,
  input  [2:0] opType,
  input  BrEq,
  input  BrLT,
  output BSel,
  output PCSel,
  output BrUn,
  output ASel,
  output RegWEn,
  output MemRW,
  output [1:0] WBSel,
  output [3:0] ALUSel
);

  wire and_1_out, andi_out, beq_out, blt_out, bltu_out, bne_out, comparator_1_eq, comparator_2_eq,
       comparator_3_eq, comparator_4_eq, comparator_5_eq, comparator_6_eq, comparator_7_eq, comparator_8_eq,
       comparator_9_eq, comparator_9_lt, comparator_10_eq, comparator_11_eq, comparator_11_lt,
       comparator_12_eq, comparator_13_eq, comparator_14_eq, comparator_15_eq, comparator_16_eq,
       comparator_17_eq, comparator_18_eq, comparator_19_eq, comparator_20_eq, comparator_21_eq,
       comparator_22_eq, comparator_23_eq, comparator_24_eq, comparator_25_eq, comparator_26_eq,
       comparator_27_eq, comparator_28_eq, comparator_29_eq, comparator_30_eq, comparator_31_eq,
       comparator_32_eq, comparator_33_eq, comparator_34_eq, comparator_35_eq, multiplexer_1_out, not_1_out,
       not_3_out, or_1_out, or_4_out, or_5_out, or_6_out, ori_out, slli_out, slti_out, srli_out, xori_out;

  Comparator #(.width(3)) comparator_1 (.a(opType), .b(3'b100), .eq(comparator_1_eq));  // open: gt, lt
  Comparator #(.width(3)) comparator_2 (.a(opType), .b(3'b101), .eq(comparator_2_eq));  // open: gt, lt
  Comparator #(.width(3)) comparator_3 (.a(opType), .b(3'b110), .eq(comparator_3_eq));  // open: gt, lt
  Comparator #(.width(3)) comparator_4 (.a(opType), .b(3'b111), .eq(comparator_4_eq));  // open: gt, lt
  Comparator #(.width(3)) comparator_5 (.a(funct3), .b(3'b000), .eq(comparator_5_eq));  // open: gt, lt
  Comparator #(.width(3)) comparator_6 (.a(funct3), .b(3'b110), .eq(comparator_6_eq));  // open: gt, lt
  Comparator #(.width(3)) comparator_7 (.a(funct3), .b(3'b100), .eq(comparator_7_eq));  // open: gt, lt
  Comparator #(.width(3)) comparator_8 (.a(funct3), .b(3'b001), .eq(comparator_8_eq));  // open: gt, lt
  not not_1 (not_1_out, BrEq);
  and beq (beq_out, comparator_5_eq, BrEq);
  and bltu (bltu_out, comparator_6_eq, BrLT);
  and blt (blt_out, comparator_7_eq, BrLT);
  and bne (bne_out, comparator_8_eq, not_1_out);
  Comparator #(.width(3)) comparator_9 (
    .a(opType), .b(3'b000), .eq(comparator_9_eq), .lt(comparator_9_lt));  // open: gt
  Comparator #(.width(3)) comparator_10 (.a(opType), .b(3'b001), .eq(comparator_10_eq));  // open: gt, lt
  Comparator #(.width(3)) comparator_11 (
    .a(opType), .b(3'b010), .eq(comparator_11_eq), .lt(comparator_11_lt));  // open: gt
  Comparator #(.width(3)) comparator_12 (.a(opType), .b(3'b011), .eq(comparator_12_eq));  // open: gt, lt
  Comparator #(.width(32)) comparator_13 (.a(Inst32), .b({32{1'b0}}), .eq(comparator_13_eq));  // open: gt, lt
  or or_1 (or_1_out, beq_out, bltu_out, blt_out, bne_out);
  Multiplexer #(.enable("false")) multiplexer_1 (.in0(1'b1), .in1(1'b0), .out(multiplexer_1_out), .sel(and_1_out));
  and and_1 (and_1_out, comparator_9_eq, or_1_out);
  and and_2 (BrUn, comparator_9_eq, bltu_out);
  or or_2 (ASel, comparator_9_eq, comparator_11_eq);
  and and_3 (MemRW, comparator_3_eq, comparator_14_eq);
  Comparator #(.width(3)) comparator_14 (.a(funct3), .b(3'b010), .eq(comparator_14_eq));  // open: gt, lt
  not not_2 (BSel, comparator_4_eq);
  or or_3 (PCSel, multiplexer_1_out, comparator_13_eq);
  nor nor_1 (RegWEn, comparator_9_eq, MemRW);
  not not_3 (not_3_out, BSel);
  or or_4 (or_4_out, comparator_11_eq, comparator_12_eq);
  or or_5 (or_5_out, comparator_2_eq, not_3_out);
  Comparator #(.width(20)) comparator_15 (
    .a({1'b0, opcode, 1'b0, funct3, 1'b0, funct7}), .b(20'h33000), .eq(comparator_15_eq));  // open: gt, lt
  Comparator #(.width(20)) comparator_16 (
    .a({1'b0, opcode, 1'b0, funct3, 1'b0, funct7}), .b(20'h13000), .eq(comparator_16_eq));  // open: gt, lt
  Comparator #(.width(20)) comparator_17 (
    .a({1'b0, opcode, 1'b0, funct3, 1'b0, funct7}), .b(20'h33700), .eq(comparator_17_eq));  // open: gt, lt
  Comparator #(.width(12)) comparator_18 (
    .a({1'b0, opcode, 1'b0, funct3}), .b(12'h137), .eq(comparator_18_eq));  // open: gt, lt
  Comparator #(.width(20)) comparator_19 (
    .a({1'b0, opcode, 1'b0, funct3, 1'b0, funct7}), .b(20'h33600), .eq(comparator_19_eq));  // open: gt, lt
  Comparator #(.width(12)) comparator_20 (
    .a({1'b0, opcode, 1'b0, funct3}), .b(12'h136), .eq(comparator_20_eq));  // open: gt, lt
  Comparator #(.width(20)) comparator_21 (
    .a({1'b0, opcode, 1'b0, funct3, 1'b0, funct7}), .b(20'h33400), .eq(comparator_21_eq));  // open: gt, lt
  Comparator #(.width(12)) comparator_22 (
    .a({1'b0, opcode, 1'b0, funct3}), .b(12'h134), .eq(comparator_22_eq));  // open: gt, lt
  Comparator #(.width(20)) comparator_23 (
    .a({1'b0, opcode, 1'b0, funct3, 1'b0, funct7}), .b(20'h33500), .eq(comparator_23_eq));  // open: gt, lt
  Comparator #(.width(20)) comparator_24 (
    .a({1'b0, opcode, 1'b0, funct3, 1'b0, funct7}), .b(20'h13500), .eq(comparator_24_eq));  // open: gt, lt
  Priority_Encoder #(.select(2)) priority_encoder_1 (
    .in0(or_5_out), .in1(comparator_1_eq), .in2(or_4_out), .out(WBSel));  // open: in3, gs, en_out, en_in
  or andi (andi_out, comparator_17_eq, comparator_18_eq);
  or ori (ori_out, comparator_19_eq, comparator_20_eq);
  or xori (xori_out, comparator_21_eq, comparator_22_eq);
  or srli (srli_out, comparator_23_eq, comparator_24_eq);
  or or_6 (or_6_out, comparator_10_eq, comparator_9_eq, comparator_11_eq, comparator_12_eq, comparator_1_eq, comparator_3_eq, comparator_15_eq, comparator_16_eq);
  Comparator #(.width(20)) comparator_25 (
    .a({1'b0, opcode, 1'b0, funct3, 1'b0, funct7}), .b(20'h13520), .eq(comparator_25_eq));  // open: gt, lt
  Comparator #(.width(20)) comparator_26 (
    .a({1'b0, opcode, 1'b0, funct3, 1'b0, funct7}), .b(20'h33100), .eq(comparator_26_eq));  // open: gt, lt
  Comparator #(.width(12)) comparator_27 (
    .a({1'b0, opcode, 1'b0, funct3}), .b(12'h131), .eq(comparator_27_eq));  // open: gt, lt
  Comparator #(.width(20)) comparator_28 (
    .a({1'b0, opcode, 1'b0, funct3, 1'b0, funct7}), .b(20'h33200), .eq(comparator_28_eq));  // open: gt, lt
  Comparator #(.width(12)) comparator_29 (
    .a({1'b0, opcode, 1'b0, funct3}), .b(12'h132), .eq(comparator_29_eq));  // open: gt, lt
  Comparator #(.width(20)) comparator_30 (
    .a({1'b0, opcode, 1'b0, funct3, 1'b0, funct7}), .b(20'h33501), .eq(comparator_30_eq));  // open: gt, lt
  Comparator #(.width(20)) comparator_31 (
    .a({1'b0, opcode, 1'b0, funct3, 1'b0, funct7}), .b(20'h33701), .eq(comparator_31_eq));  // open: gt, lt
  Comparator #(.width(20)) comparator_32 (
    .a({1'b0, opcode, 1'b0, funct3, 1'b0, funct7}), .b(20'h33001), .eq(comparator_32_eq));  // open: gt, lt
  Comparator #(.width(20)) comparator_33 (
    .a({1'b0, opcode, 1'b0, funct3, 1'b0, funct7}), .b(20'h33301), .eq(comparator_33_eq));  // open: gt, lt
  or slli (slli_out, comparator_26_eq, comparator_27_eq);
  or slti (slti_out, comparator_28_eq, comparator_29_eq);
  Comparator #(.width(20)) comparator_34 (
    .a({1'b0, opcode, 1'b0, funct3, 1'b0, funct7}), .b(20'h33020), .eq(comparator_34_eq));  // open: gt, lt
  Comparator #(.width(20)) comparator_35 (
    .a({1'b0, opcode, 1'b0, funct3, 1'b0, funct7}), .b(20'h33101), .eq(comparator_35_eq));  // open: gt, lt
  Priority_Encoder #(.select(4)) priority_encoder_2 (
    .in0(or_6_out), .in1(andi_out), .in2(ori_out), .in3(xori_out), .in4(srli_out), .in5(comparator_25_eq),
    .in6(slli_out), .in7(slti_out), .in8(comparator_30_eq), .in9(comparator_31_eq), .in10(comparator_32_eq),
    .in11(comparator_33_eq), .in12(comparator_34_eq), .in14(comparator_35_eq), .out(ALUSel));  // open: in13, in15, gs, en_out, en_in

  // Other names for the same wires on the sheet: LongInst (some bits) = {opcode, funct3, funct7};
  //   ShortInst (some bits) = {opcode, funct3}
endmodule

module BranchComp (
  input  [31:0] DataA,
  input  [31:0] DataB,
  input  BrUn,
  output BrEq,
  output BrLT
);

  wire comparator_1_eq, comparator_1_lt, comparator_2_eq, comparator_2_lt;

  Comparator #(.width(32), .mode("unsigned")) comparator_1 (
    .a(DataA), .b(DataB), .eq(comparator_1_eq), .lt(comparator_1_lt));  // open: gt
  Comparator #(.width(32)) comparator_2 (.a(DataA), .b(DataB), .eq(comparator_2_eq), .lt(comparator_2_lt));  // open: gt
  Multiplexer #(.enable("false")) multiplexer_1 (.in0(comparator_1_eq), .in1(comparator_2_eq), .out(BrEq), .sel(BrUn));
  Multiplexer #(.enable("false")) multiplexer_2 (.in0(comparator_1_lt), .in1(comparator_2_lt), .out(BrLT), .sel(BrUn));
endmodule
